// Logisim project EP02.circ as structural Verilog: 8 circuits, main circuit main
module main (
);

  ULA_1_bit ula_1_bit_1 ();  // open: A, B, Result, BInvert, Carry_In, Carry_Out, OP1, OP0
endmodule

// ULA
module ULA_1_bit (
  input  BInvert,
  input  Carry_In,
  input  A,
  input  B,
  input  OP1,
  input  OP0,
  output Result,
  output Carry_Out
);

  wire and_1_out, fulladder_1_sum, mux_2x1_1_s0, not_1_out, not_2_out, or_1_out;

  MUX_2x1 mux_2x1_1 (.I0(B), .I1(not_1_out), .S0(mux_2x1_1_s0), .A0(BInvert));
  not not_1 (not_1_out, B);
  not not_2 (not_2_out, A);
  and and_1 (and_1_out, A, mux_2x1_1_s0);
  or or_1 (or_1_out, A, mux_2x1_1_s0);
  FULLADDER fulladder_1 (.Carry_In(Carry_In), .I0(A), .I1(mux_2x1_1_s0), .Sum(fulladder_1_sum), .Carry_Out(Carry_Out));
  MUX_4x2 mux_4x2_1 (
    .I1(and_1_out), .I2(or_1_out), .I3(not_2_out), .I4(fulladder_1_sum), .S0(Result), .A1(OP1), .A0(OP0));

  // Notes on the sheet:
  //   A  B  Result$0  0   A & B$0  1   A | B$1  0   A'$1  1   sum(A,B)$
endmodule

module ULA_4_bits (
  input  B3,
  input  B2,
  input  B1,
  input  B0,
  input  A3,
  input  A2,
  input  A1,
  input  A0,
  input  BInvert,
  input  OP1,
  input  OP0,
  output S0,
  output S1,
  output S2,
  output S3,
  output Carry_Out
);

  wire ula_1_bit_1_carry_out, ula_1_bit_2_carry_out, ula_1_bit_3_carry_out;

  ULA_1_bit ula_1_bit_1 (
    .A(A0), .B(B0), .Result(S0), .BInvert(BInvert), .Carry_In(BInvert), .Carry_Out(ula_1_bit_1_carry_out),
    .OP1(OP1), .OP0(OP0));
  ULA_1_bit ula_1_bit_2 (
    .A(A1), .B(B1), .Result(S1), .BInvert(BInvert), .Carry_In(ula_1_bit_1_carry_out),
    .Carry_Out(ula_1_bit_2_carry_out), .OP1(OP1), .OP0(OP0));
  ULA_1_bit ula_1_bit_3 (
    .A(A2), .B(B2), .Result(S2), .BInvert(BInvert), .Carry_In(ula_1_bit_2_carry_out),
    .Carry_Out(ula_1_bit_3_carry_out), .OP1(OP1), .OP0(OP0));
  ULA_1_bit ula_1_bit_4 (
    .A(A3), .B(B3), .Result(S3), .BInvert(BInvert), .Carry_In(ula_1_bit_3_carry_out), .Carry_Out(Carry_Out),
    .OP1(OP1), .OP0(OP0));
endmodule

module ULA_74LS181 (
  input  [3:0] A,
  input  [3:0] B,
  input  [3:0] in_3,
  output [3:0] S
);

  wire [3:0] and_1_out, and_2_out, and_3_out, nand_1_out, nor_1_out, not_1_out, not_2_out, not_3_out,
       not_4_out, not_5_out, not_6_out, or_1_out, or_2_out, or_3_out, xnor_1_out;

  assign not_1_out = ~A;  // NOT_Gate not_1, 4 bits wide
  assign nor_1_out = ~(A | B);  // NOR_Gate nor_1, 4 bits wide
  assign not_2_out = ~A;  // NOT_Gate not_2, 4 bits wide
  assign and_1_out = not_2_out & B;  // AND_Gate and_1, 4 bits wide
  assign nand_1_out = ~(A & B);  // NAND_Gate nand_1, 4 bits wide
  assign not_3_out = ~B;  // NOT_Gate not_3, 4 bits wide
  // XOR_Gate xor_1 has open pins: in0=A, in1=B, out=open
  assign and_2_out = A & not_4_out;  // AND_Gate and_2, 4 bits wide
  assign not_4_out = ~B;  // NOT_Gate not_4, 4 bits wide
  assign not_5_out = ~A;  // NOT_Gate not_5, 4 bits wide
  assign or_1_out = not_5_out | B;  // OR_Gate or_1, 4 bits wide
  assign xnor_1_out = ~(A ^ B);  // XNOR_Gate xnor_1, 4 bits wide
  assign and_3_out = A & B;  // AND_Gate and_3, 4 bits wide
  assign or_2_out = A | not_6_out;  // OR_Gate or_2, 4 bits wide
  assign not_6_out = ~B;  // NOT_Gate not_6, 4 bits wide
  assign or_3_out = A | B;  // OR_Gate or_3, 4 bits wide
  Multiplexer #(.select(4), .width(4), .enable("false")) multiplexer_1 (
    .out(S), .sel(in_3));  // open: in0, in1, in2, in3, in4, in5, in6, in7, in8, in9, in10, in11, in12, in13, in14, in15

  // Notes on the sheet:
  //   a'
  //   (a+b)'
  //   a'.b
  //   (a.b)'
  //   b'
  //   a^b
  //   a.b'
  //   a'+b
  //   1
  //   (a^b)'
  //   b
  //   a.b
  //   a+b'
  //   a+b
  //   A
endmodule

// M_2x1
module MUX_2x1 (
  input  I0,
  input  I1,
  input  A0,
  output S0
);

  wire AND1_out, AND2_out, not_1_out;

  and AND1 (AND1_out, I0, not_1_out);
  not not_1 (not_1_out, A0);
  and AND2 (AND2_out, I1, A0);
  or OR1 (S0, AND1_out, AND2_out);

  // Notes on the sheet:
  //   Multiplexador 2x1
endmodule

// M_4x2
module MUX_4x2 (
  input  A1,
  input  A0,
  input  I1,
  input  I2,
  input  I3,
  input  I4,
  output S0
);

  wire AND1_out, AND2_out, AND3_out, AND4_out, not_1_out, not_2_out;

  not not_1 (not_1_out, A1);
  not not_2 (not_2_out, A0);
  and AND1 (AND1_out, not_2_out, not_1_out, I1);
  and AND2 (AND2_out, A0, not_1_out, I2);
  and AND3 (AND3_out, not_2_out, A1, I3);
  and AND4 (AND4_out, A0, A1, I4);
  or OR1 (S0, AND1_out, AND2_out, AND3_out, AND4_out);

  // Notes on the sheet:
  //   Multiplexador 4x2
endmodule

// HA
module HALFADDER (
  input  I0,
  input  I1,
  output Sum,
  output Carry_Out
);

  xor XOR1 (Sum, I0, I1);
  and AND1 (Carry_Out, I0, I1);

  // Notes on the sheet:
  //   Compact Half Adder
endmodule

// FA
module FULLADDER (
  input  Carry_In,
  input  I0,
  input  I1,
  output Sum,
  output Carry_Out
);

  wire halfadder_1_carry_out, halfadder_1_sum, halfadder_2_carry_out;

  HALFADDER halfadder_1 (.I0(I0), .I1(I1), .Sum(halfadder_1_sum), .Carry_Out(halfadder_1_carry_out));
  HALFADDER halfadder_2 (.I0(Carry_In), .I1(halfadder_1_sum), .Sum(Sum), .Carry_Out(halfadder_2_carry_out));
  or OR1 (Carry_Out, halfadder_2_carry_out, halfadder_1_carry_out);

  // Notes on the sheet:
  //   Ful Adder
endmodule
